// Logisim project fsm.circ as structural Verilog: 1 circuit, main circuit main
module main (
  input  Clock,
  input  RESET,
  input  Start,
  input  eq_bulunan,
  input  miss_eq_10,
  input  lt_bulunan,
  input  miss_lt_10,
  input  button,
  input  eq,
  input  print,
  output [3:0] STATE,
  output e_bulunan,
  output tty_enable,
  output e_miss,
  output word_enable,
  output word_mux_enable,
  output bulunan_mux,
  output miss_mux,
  output c_count,
  output clear,
  output tty_c_count
);

  wire and_2_out, and_4_out, and_8_out, and_9_out, and_10_out, and_11_out, and_12_out, and_13_out,
       and_14_out, and_15_out, and_16_out, and_17_out, and_18_out, and_19_out, and_20_out, and_21_out,
       and_22_out, and_23_out, and_24_out, and_25_out, and_26_out, xor_1_out, xor_2_out;
  wire [3:0] or_6_out;

  Register #(.width(4)) register_1 (.D(or_6_out), .en(1'b1), .Q(STATE), .clk(Clock), .clr(RESET));
  and and_1 (or_6_out[3], ~STATE[3], STATE[2], STATE[1], ~STATE[0], eq);  // AND_Gate
  xor xor_1 (xor_1_out, miss_eq_10, miss_lt_10);
  xor xor_2 (xor_2_out, eq_bulunan, lt_bulunan);
  and and_2 (and_2_out, ~STATE[3], ~STATE[2], ~STATE[1], STATE[0]);  // AND_Gate
  and and_3 (bulunan_mux, STATE[3], ~STATE[2], ~STATE[1], ~STATE[0]);  // AND_Gate
  and and_4 (and_4_out, ~STATE[3], ~STATE[2], ~STATE[1], STATE[0]);  // AND_Gate
  and and_5 (c_count, ~STATE[3], STATE[2], STATE[1], STATE[0]);  // AND_Gate
  and and_6 (word_enable, ~STATE[3], STATE[2], ~STATE[1], STATE[0]);  // AND_Gate
  and and_7 (clear, ~STATE[3], ~STATE[2], ~STATE[1], STATE[0]);  // AND_Gate
  and and_8 (and_8_out, ~STATE[3], STATE[2], ~STATE[1], STATE[0], ~button);  // AND_Gate
  and and_9 (and_9_out, ~STATE[3], STATE[2], STATE[1], ~STATE[0], ~eq);  // AND_Gate
  and and_10 (and_10_out, ~STATE[3], ~STATE[2], STATE[1], STATE[0]);  // AND_Gate
  and and_11 (and_11_out, ~STATE[3], STATE[2], ~STATE[1], ~STATE[0]);  // AND_Gate
  and and_12 (and_12_out, ~STATE[3], ~STATE[2], STATE[1], ~STATE[0], ~eq_bulunan, lt_bulunan, xor_1_out);  // AND_Gate
  and and_13 (and_13_out, ~STATE[3], STATE[2], ~STATE[1], STATE[0]);  // AND_Gate
  and and_14 (and_14_out, ~STATE[3], STATE[2], STATE[1], ~STATE[0], ~eq);  // AND_Gate
  and and_15 (and_15_out, ~STATE[3], ~STATE[2], ~STATE[1], STATE[0]);  // AND_Gate
  and and_16 (and_16_out, ~STATE[3], ~STATE[2], STATE[1], ~STATE[0], eq_bulunan, ~miss_eq_10, ~lt_bulunan, miss_lt_10);  // AND_Gate
  and and_17 (and_17_out, ~STATE[3], STATE[2], STATE[1], STATE[0]);  // AND_Gate
  and and_18 (and_18_out, STATE[3], ~STATE[2], ~STATE[1], ~STATE[0]);  // AND_Gate
  and and_19 (and_19_out, ~STATE[3], STATE[2], ~STATE[1], STATE[0], button);  // AND_Gate
  and and_20 (and_20_out, ~STATE[3], STATE[2], STATE[1], ~STATE[0], ~eq);  // AND_Gate
  and and_21 (and_21_out, ~STATE[3], ~STATE[2], ~STATE[1], ~STATE[0], Start);  // AND_Gate
  and and_22 (and_22_out, ~STATE[3], ~STATE[2], STATE[1], ~STATE[0], ~miss_eq_10, miss_lt_10, xor_2_out);  // AND_Gate
  and and_23 (and_23_out, ~STATE[3], STATE[2], ~STATE[1], ~STATE[0], ~print);  // AND_Gate
  or or_1 (or_6_out[2], and_12_out, and_13_out, and_23_out, and_14_out);
  and and_24 (and_24_out, ~STATE[3], ~STATE[2], STATE[1], STATE[0], ~print);  // AND_Gate
  or or_2 (e_bulunan, and_2_out, bulunan_mux);
  and and_25 (and_25_out, ~STATE[3], ~STATE[2], STATE[1], STATE[0]);  // AND_Gate
  or or_3 (e_miss, and_4_out, c_count);
  and and_26 (and_26_out, ~STATE[3], STATE[2], ~STATE[1], ~STATE[0]);  // AND_Gate
  or or_4 (tty_c_count, and_10_out, and_11_out);
  or or_5 (or_6_out[1], and_15_out, and_16_out, and_17_out, and_24_out, and_18_out, and_19_out, and_20_out);
  or or_6 (or_6_out[0], and_21_out, and_8_out, and_24_out, and_9_out, and_22_out);
  or or_7 (tty_enable, bulunan_mux, and_26_out, and_25_out);

  assign miss_mux = c_count;
  assign word_mux_enable = word_enable;
endmodule
