// Logisim project test.circ as structural Verilog: 1 circuit, main circuit main
module main (
  input  [31:0] in_1,
  input  [31:0] in_2,
  output [3:0] out_3
);

  wire A_out, and_1_out, and_2_out, and_3_out, and_5_out, and_6_out, and_7_out, B_out, C_out, clock_1_out,
       clock_2_out, clock_3_out, D_out, E_out, F_out, G_out, H_out, I_out, J_out, K_out, L_out, M_out,
       main_1_bulunan_mux, main_1_c_count, main_1_clear, main_1_e_bulunan, main_1_e_miss, main_1_miss_mux,
       main_1_tty_c_count, main_1_tty_enable, main_1_word_enable, main_1_word_mux_enable, main_2_button,
       main_2_eq, main_2_eq_bulunan, main_2_led1, main_2_led2, main_2_led3, main_2_led4, main_2_led5,
       main_2_led6, main_2_led7, main_2_led8, main_2_led9, main_2_led10, main_2_lt_bulunan,
       main_2_miss_eq_10, main_2_miss_lt_10, main_2_print, main_3_fifth, main_3_first, main_3_fourth,
       main_3_second, main_3_seventh, main_3_sixth, main_3_third, main_4_fifth, main_4_first, main_4_fourth,
       main_4_second, main_4_seventh, main_4_sixth, main_4_third, main_5_fifth, main_5_first, main_5_fourth,
       main_5_second, main_5_seventh, main_5_sixth, main_5_third, N_out, not_1_out, not_2_out, not_3_out,
       not_4_out, not_5_out, not_6_out, not_7_out, not_8_out, not_9_out, not_10_out, O_out, P_out, Q_out,
       R_out, RESET_out, S_out, START_out, T_out, U_out, V_out, W_out, X_out, Y_out, Z_out;
  wire [1:0] and_4_out, and_8_out, State_2_q, State_q;
  wire [3:0] counter_1_q, counter_2_q, main_2__7_segment_output, subtractor_1_out;
  wire [6:0] main_2_tty_input;

  Clock clock_1 (.out(clock_1_out));
  Button A (.out(A_out));
  Button B (.out(B_out));
  Button C (.out(C_out));
  Button D (.out(D_out));
  Button START (.out(START_out));
  Button RESET (.out(RESET_out));
  Button E (.out(E_out));
  Button F (.out(F_out));
  Button G (.out(G_out));
  Button H (.out(H_out));
  fsm_main main_1 (
    .Clock(clock_1_out), .RESET(RESET_out), .Start(START_out), .eq_bulunan(main_2_eq_bulunan),
    .miss_eq_10(main_2_miss_eq_10), .lt_bulunan(main_2_lt_bulunan), .miss_lt_10(main_2_miss_lt_10),
    .button(main_2_button), .eq(main_2_eq), .print(main_2_print), .STATE(out_3),
    .e_bulunan(main_1_e_bulunan), .tty_enable(main_1_tty_enable), .e_miss(main_1_e_miss),
    .word_enable(main_1_word_enable), .word_mux_enable(main_1_word_mux_enable),
    .bulunan_mux(main_1_bulunan_mux), .miss_mux(main_1_miss_mux), .c_count(main_1_c_count),
    .clear(main_1_clear), .tty_c_count(main_1_tty_c_count));
  Button I (.out(I_out));
  Button J (.out(J_out));
  Button K (.out(K_out));
  Button L (.out(L_out));
  Button M (.out(M_out));
  Button N (.out(N_out));
  Button O (.out(O_out));
  Button P (.out(P_out));
  Button Q (.out(Q_out));
  Button R (.out(R_out));
  Button S (.out(S_out));
  Button T (.out(T_out));
  Button U (.out(U_out));
  Button V (.out(V_out));
  Button W (.out(W_out));
  Button X (.out(X_out));
  Button Y (.out(Y_out));
  Button Z (.out(Z_out));
  datapath_main main_2 (
    .tty_c_count(main_1_tty_c_count), .tty_enable(main_1_tty_enable), .word_enable(main_1_word_enable),
    .First(in_1), .Second(in_2), .bulunan_mux(main_1_bulunan_mux), .e_bulunan(main_1_e_bulunan),
    .Clock(clock_1_out), .A(A_out), .miss_mux(main_1_miss_mux), .B(B_out), .e_miss(main_1_e_miss), .C(C_out),
    .D(D_out), .E(E_out), .F(F_out), .G(G_out), .H(H_out), .I(I_out), .J(J_out), .K(K_out), .L(L_out),
    .c_count(main_1_c_count), .M(M_out), .N(N_out), .word_mux_enable(main_1_word_mux_enable), .O(O_out),
    .P(P_out), .Q(Q_out), .R(R_out), .S(S_out), .T(T_out), .U(U_out), .V(V_out), .W(W_out), .X(X_out),
    .Y(Y_out), .Z(Z_out), .clear(main_1_clear), .eq(main_2_eq), .print(main_2_print),
    .tty_input(main_2_tty_input), ._7_segment_output(main_2__7_segment_output),
    .eq_bulunan(main_2_eq_bulunan), .lt_bulunan(main_2_lt_bulunan), .miss_eq_10(main_2_miss_eq_10),
    .miss_lt_10(main_2_miss_lt_10), .button(main_2_button), .led1(main_2_led1), .led2(main_2_led2),
    .led3(main_2_led3), .led4(main_2_led4), .led5(main_2_led5), .led6(main_2_led6), .led7(main_2_led7),
    .led8(main_2_led8), .led9(main_2_led9), .led10(main_2_led10));  // open: lose_c
  TTY tty_1 (.data(main_2_tty_input), .clk(clock_1_out), .we(main_1_tty_enable), .clr(main_1_clear));
  _7_Segment_Display_main main_3 (
    .Number(main_2__7_segment_output), .First(main_3_first), .Second(main_3_second), .Third(main_3_third),
    .Fourth(main_3_fourth), .Fifth(main_3_fifth), .Sixth(main_3_sixth), .Seventh(main_3_seventh));
  LED led_1 (.in(main_2_led1));
  LED led_2 (.in(main_2_led2));
  LED led_3 (.in(main_2_led3));
  LED led_4 (.in(main_2_led4));
  LED led_5 (.in(main_2_led5));
  LED led_6 (.in(main_2_led6));
  LED led_7 (.in(main_2_led7));
  LED led_8 (.in(main_2_led8));
  LED led_9 (.in(main_2_led9));
  LED led_10 (.in(main_2_led10));
  _7_Segment_Display u_7_segment_display_1 (
    .g(main_3_seventh), .f(main_3_sixth), .a(main_3_first), .b(main_3_second), .e(main_3_fifth),
    .d(main_3_fourth), .c(main_3_third));  // open: dp
  _7_Segment_Display_main main_4 (
    .Number(counter_2_q), .First(main_4_first), .Second(main_4_second), .Third(main_4_third),
    .Fourth(main_4_fourth), .Fifth(main_4_fifth), .Sixth(main_4_sixth), .Seventh(main_4_seventh));
  _7_Segment_Display u_7_segment_display_2 (
    .g(main_4_seventh), .f(main_4_sixth), .a(main_4_first), .b(main_4_second), .e(main_4_fifth),
    .d(main_4_fourth), .c(main_4_third));  // open: dp
  _7_Segment_Display_main main_5 (
    .Number(subtractor_1_out), .First(main_5_first), .Second(main_5_second), .Third(main_5_third),
    .Fourth(main_5_fourth), .Fifth(main_5_fifth), .Sixth(main_5_sixth), .Seventh(main_5_seventh));
  _7_Segment_Display u_7_segment_display_3 (
    .g(main_5_seventh), .f(main_5_sixth), .a(main_5_first), .b(main_5_second), .e(main_5_fifth),
    .d(main_5_fourth), .c(main_5_third));  // open: dp
  Counter #(.width(4), .max('hf)) counter_1 (
    .count(and_1_out), .Q(counter_1_q), .clk(clock_1_out));  // open: load, D, carry, clr
  Counter #(.width(4), .max('hf)) counter_2 (
    .count(and_5_out), .Q(counter_2_q), .clk(clock_1_out));  // open: load, D, carry, clr
  Subtractor #(.width(4)) subtractor_1 (.a(counter_1_q), .b(4'b0001), .out(subtractor_1_out));  // open: bin, bout
  Clock clock_2 (.out(clock_2_out));
  Clock clock_3 (.out(clock_3_out));
  Register #(.width(2)) State (.D(and_4_out), .en(1'b1), .Q(State_q), .clk(clock_2_out));  // open: clr
  Register #(.width(2)) State_2 (.D(and_8_out), .en(1'b1), .Q(State_2_q), .clk(clock_3_out));  // open: clr
  not not_1 (not_1_out, State_q[1]);
  not not_2 (not_2_out, State_q[1]);
  not not_3 (not_3_out, State_q[0]);
  not not_4 (not_4_out, State_q[0]);
  not not_5 (not_5_out, State_q[1]);
  not not_6 (not_6_out, State_2_q[1]);
  not not_7 (not_7_out, State_2_q[1]);
  not not_8 (not_8_out, State_2_q[0]);
  not not_9 (not_9_out, State_2_q[0]);
  not not_10 (not_10_out, State_2_q[1]);
  and and_1 (and_1_out, not_1_out, State_q[0]);
  and and_2 (and_2_out, main_2_eq_bulunan, not_2_out, State_q[0]);
  and and_3 (and_3_out, main_2_eq_bulunan, not_3_out, State_q[1]);
  and and_4 (and_4_out[0], main_2_eq_bulunan, not_4_out, not_5_out);
  and and_5 (and_5_out, not_6_out, State_2_q[0]);
  and and_6 (and_6_out, main_2_led10, not_7_out, State_2_q[0]);
  and and_7 (and_7_out, main_2_led10, not_8_out, State_2_q[1]);
  and and_8 (and_8_out[0], main_2_led10, not_9_out, not_10_out);
  or or_1 (and_4_out[1], and_2_out, and_3_out);
  or or_2 (and_8_out[1], and_6_out, and_7_out);

  // Notes on the sheet:
  //   NUMBER OF WORD
  //   MACHİNE
  //   USER
  //   n0
  //   n0
endmodule
