// Logisim project control_unit.circ as structural Verilog: 1 circuit, main circuit main
module main (
  input  lt,
  input  start,
  input  gt,
  input  eq,
  input  Clock,
  output L_mult,
  output S_mult,
  output L_a,
  output C_load,
  output S_a,
  output C_count,
  output [2:0] state
);

  wire and_1_out, and_2_out, and_3_out, and_4_out, and_9_out, and_10_out, and_11_out, not_1_out, not_2_out,
       not_3_out, not_4_out, not_5_out, not_6_out, not_7_out, not_8_out, not_9_out, not_10_out, not_11_out,
       not_12_out, not_13_out, not_14_out, not_15_out, not_16_out, not_17_out, not_18_out, not_19_out,
       not_20_out, not_21_out, not_22_out, not_23_out, not_24_out, not_25_out;
  wire [2:0] or_2_out;

  Register #(.width(3)) u_State (.D(or_2_out), .en(1'b1), .Q(state), .clk(Clock));  // open: clr
  not not_1 (not_1_out, state[2]);
  not not_2 (not_2_out, state[0]);
  not not_3 (not_3_out, lt);
  not not_4 (not_4_out, eq);
  not not_5 (not_5_out, state[2]);
  not not_6 (not_6_out, state[1]);
  not not_7 (not_7_out, state[0]);
  not not_8 (not_8_out, state[2]);
  not not_9 (not_9_out, state[0]);
  not not_10 (not_10_out, lt);
  not not_11 (not_11_out, eq);
  not not_12 (not_12_out, state[2]);
  not not_13 (not_13_out, state[1]);
  not not_14 (not_14_out, state[2]);
  not not_15 (not_15_out, state[2]);
  not not_16 (not_16_out, state[2]);
  not not_17 (not_17_out, state[1]);
  not not_18 (not_18_out, state[0]);
  not not_19 (not_19_out, state[2]);
  not not_20 (not_20_out, state[1]);
  not not_21 (not_21_out, state[0]);
  not not_22 (not_22_out, state[2]);
  not not_23 (not_23_out, state[1]);
  and and_1 (and_1_out, not_1_out, state[1], not_2_out, not_3_out, gt, not_4_out);
  and and_2 (and_2_out, not_5_out, not_6_out, not_7_out, start);
  and and_3 (and_3_out, not_8_out, state[1], not_9_out, not_10_out, gt, not_11_out);
  and and_4 (and_4_out, not_12_out, not_13_out, state[0]);
  not not_24 (not_24_out, state[1]);
  not not_25 (not_25_out, state[0]);
  and and_5 (or_2_out[2], not_14_out, state[1], state[0]);
  and and_6 (L_mult, not_15_out, state[0]);
  and and_7 (C_count, not_16_out, state[1], state[0]);
  and and_8 (S_a, state[2], not_17_out, not_18_out);
  and and_9 (and_9_out, not_19_out, not_20_out, not_21_out);
  or or_1 (L_a, S_a, and_9_out);
  and and_10 (and_10_out, not_22_out, not_23_out, state[0]);
  and and_11 (and_11_out, state[2], not_24_out, not_25_out);
  or or_2 (or_2_out[0], and_1_out, and_2_out);
  or or_3 (or_2_out[1], and_3_out, and_11_out, and_4_out);
  or or_4 (C_load, and_10_out, C_count);

  assign S_mult = C_count;
endmodule
