// Logisim project datapath.circ as structural Verilog: 1 circuit, main circuit main
module main (
  input  S_mult,
  input  [15:0] Input_b,
  input  [31:0] _0_Register,
  input  L_mult,
  input  [15:0] Input_a,
  input  L_a,
  input  Clock,
  input  [31:0] _0_Register_2,
  input  S_a,
  input  C_load,
  input  C_count,
  output gt,
  output eq,
  output lt,
  output [31:0] Mult
);

  wire [31:0] a_q, adder_1_out, bit_extender_1_out, bit_extender_2_out, counter_1_q, multiplexer_1_out,
       multiplexer_2_out, register_1_q, register_2_q;

  Register #(.width(32)) register_1 (.D(_0_Register), .en(1'b1), .Q(register_1_q), .clk(Clock));  // open: clr
  assign bit_extender_1_out = {{16{1'b0}}, Input_a};  // Bit_Extender bit_extender_1
  assign bit_extender_2_out = {{16{1'b0}}, Input_b};  // Bit_Extender bit_extender_2
  Multiplexer #(.width(32), .enable("false")) multiplexer_1 (
    .in0(register_1_q), .in1(adder_1_out), .out(multiplexer_1_out), .sel(S_mult));
  Register #(.width(32)) u_MULT (.D(multiplexer_1_out), .en(L_mult), .Q(Mult), .clk(Clock));  // open: clr
  Multiplexer #(.width(32), .enable("false")) multiplexer_2 (
    .in0(bit_extender_1_out), .in1(counter_1_q), .out(multiplexer_2_out), .sel(S_a));
  Register #(.width(32)) a (.D(multiplexer_2_out), .en(L_a), .Q(a_q), .clk(Clock));  // open: clr
  Counter #(.width(32), .max('hffffffff)) counter_1 (
    .load(C_load), .D(a_q), .count(C_count), .Q(counter_1_q), .clk(Clock));  // open: carry, clr
  Adder #(.width(32)) adder_1 (.a(bit_extender_2_out), .b(Mult), .out(adder_1_out), .cin(1'b0));  // open: cout
  Register #(.width(32)) register_2 (.D(_0_Register_2), .en(1'b1), .Q(register_2_q), .clk(Clock));  // open: clr
  Comparator #(.width(32)) comparator_1 (.a(a_q), .b(register_2_q), .gt(gt), .eq(eq), .lt(lt));

  // Notes on the sheet:
  //   mult+b
endmodule
