// Logisim project 7 Segment Display.circ as structural Verilog: 2 circuits, main circuit main
module main (
  input  [3:0] Number,
  output First,
  output Second,
  output Third,
  output Fourth,
  output Fifth,
  output Sixth,
  output Seventh
);

  wire and_1_out, and_2_out, and_3_out, and_4_out, and_5_out, and_6_out, and_7_out, and_8_out, and_9_out,
       and_10_out, and_11_out, and_12_out, and_13_out, and_14_out, and_15_out, and_16_out, and_17_out,
       and_18_out, and_19_out, and_20_out, and_21_out, and_22_out, and_23_out, and_24_out, and_25_out,
       and_26_out, and_27_out;

  and and_1 (and_1_out, ~Number[3], Number[1]);  // AND_Gate
  and and_2 (and_2_out, Number[2], Number[0]);  // AND_Gate
  and and_3 (and_3_out, ~Number[2], ~Number[1], ~Number[0]);  // AND_Gate
  and and_4 (and_4_out, Number[3], ~Number[2], ~Number[1]);  // AND_Gate
  and and_5 (and_5_out, ~Number[3], ~Number[1], ~Number[0]);  // AND_Gate
  and and_6 (and_6_out, ~Number[2], ~Number[1], ~Number[0]);  // AND_Gate
  and and_7 (and_7_out, ~Number[3], Number[1], Number[0]);  // AND_Gate
  and and_8 (and_8_out, ~Number[3], ~Number[2], Number[1]);  // AND_Gate
  and and_9 (and_9_out, Number[3], ~Number[2], ~Number[1]);  // AND_Gate
  and and_10 (and_10_out, ~Number[3], Number[2]);  // AND_Gate
  and and_11 (and_11_out, ~Number[3], ~Number[1], ~Number[0]);  // AND_Gate
  and and_12 (and_12_out, ~Number[3], Number[1], Number[0]);  // AND_Gate
  and and_13 (and_13_out, Number[3], ~Number[2], ~Number[1]);  // AND_Gate
  and and_14 (and_14_out, ~Number[3], Number[2], ~Number[1], Number[0]);  // AND_Gate
  and and_15 (and_15_out, ~Number[2], ~Number[1], ~Number[0]);  // AND_Gate
  and and_16 (and_16_out, ~Number[3], ~Number[2], Number[1]);  // AND_Gate
  and and_17 (and_17_out, ~Number[3], Number[1], ~Number[0]);  // AND_Gate
  and and_18 (and_18_out, ~Number[2], ~Number[1], ~Number[0]);  // AND_Gate
  and and_19 (and_19_out, ~Number[3], ~Number[2], ~Number[1]);  // AND_Gate
  and and_20 (and_20_out, ~Number[3], Number[1], ~Number[0]);  // AND_Gate
  and and_21 (and_21_out, ~Number[3], ~Number[1]);  // AND_Gate
  and and_22 (and_22_out, Number[3], ~Number[2], ~Number[1]);  // AND_Gate
  and and_23 (and_23_out, ~Number[3], Number[2], ~Number[0], Number[1]);  // AND_Gate
  and and_24 (and_24_out, Number[3], ~Number[2], ~Number[1]);  // AND_Gate
  and and_25 (and_25_out, ~Number[3], Number[2], ~Number[1]);  // AND_Gate
  and and_26 (and_26_out, ~Number[3], ~Number[2], Number[1]);  // AND_Gate
  and and_27 (and_27_out, ~Number[3], Number[1], ~Number[0]);  // AND_Gate
  or or_1 (First, and_1_out, and_2_out, and_3_out, and_4_out);
  or or_2 (Second, and_5_out, and_6_out, and_7_out, and_8_out, and_9_out);
  or or_3 (Third, and_10_out, and_11_out, and_12_out, and_13_out);
  or or_4 (Fourth, and_14_out, and_15_out, and_16_out, and_17_out);
  or or_5 (Fifth, and_18_out, and_19_out, and_20_out);
  or or_6 (Sixth, and_21_out, and_22_out, and_23_out);
  or or_7 (Seventh, and_24_out, and_25_out, and_26_out, and_27_out);
endmodule

module _7_Segment_Display (
  input  [3:0] in_1
);

  wire main_1_fifth, main_1_first, main_1_fourth, main_1_second, main_1_seventh, main_1_sixth, main_1_third;

  main main_1 (
    .Number(in_1), .First(main_1_first), .Second(main_1_second), .Third(main_1_third),
    .Fourth(main_1_fourth), .Fifth(main_1_fifth), .Sixth(main_1_sixth), .Seventh(main_1_seventh));
  _7_Segment_Display_part u_7_segment_display_1 (
    .g(main_1_seventh), .f(main_1_sixth), .a(main_1_first), .b(main_1_second), .e(main_1_fifth),
    .d(main_1_fourth), .c(main_1_third));  // open: dp
endmodule
