// Logisim project datapath.circ as structural Verilog: 1 circuit, main circuit main
module main (
  input  tty_c_count,
  input  tty_enable,
  input  word_enable,
  input  [31:0] First,
  input  [31:0] Second,
  input  bulunan_mux,
  input  e_bulunan,
  input  Clock,
  input  A,
  input  miss_mux,
  input  B,
  input  e_miss,
  input  C,
  input  D,
  input  E,
  input  F,
  input  G,
  input  H,
  input  I,
  input  J,
  input  K,
  input  L,
  input  c_count,
  input  M,
  input  N,
  input  word_mux_enable,
  input  O,
  input  P,
  input  Q,
  input  R,
  input  S,
  input  T,
  input  U,
  input  V,
  input  W,
  input  X,
  input  Y,
  input  Z,
  input  clear,
  output eq,
  output print,
  output [6:0] tty_input,
  output [3:0] _7_segment_output,
  output eq_bulunan,
  output lt_bulunan,
  output miss_eq_10,
  output miss_lt_10,
  output button,
  output led1,
  output led2,
  output led3,
  output led4,
  output led5,
  output led6,
  output led7,
  output led8,
  output led9,
  output led10,
  output lose_c
);

  wire comparator_1_gt, comparator_2_gt, comparator_3_eq, comparator_4_eq, comparator_5_eq, comparator_6_eq,
       comparator_7_eq, comparator_8_eq, comparator_9_eq, comparator_10_eq, comparator_11_gt,
       comparator_12_gt, comparator_13_gt, comparator_14_gt, comparator_15_gt, comparator_16_gt;
  wire [3:0] adder_1_out, adder_2_out, adder_4_out, adder_5_out, adder_8_out, adder_10_out,
       bit_extender_1_out, bit_extender_2_out, bit_extender_3_out, bit_extender_4_out, bit_extender_7_out,
       bit_extender_8_out, bit_extender_9_out, bit_extender_10_out, counter_2_q;
  wire [4:0] adder_6_out, adder_7_out, adder_9_out, bit_extender_5_out, bulunan_q, c_miss_q, counter_1_q,
       multiplexer_3_out, multiplexer_4_out, Number_of_word_q;
  wire [7:0] bitselector_1_out, bitselector_2_out, bitselector_3_out, bitselector_4_out, bitselector_5_out,
       bitselector_6_out, bitselector_7_out, bitselector_8_out, controlled_buffer_1_out, multiplexer_1_out,
       multiplexer_2_out, multiplexer_5_out, register_1_q, register_2_q, register_3_q, register_4_q,
       register_5_q, register_6_q, register_7_q, register_8_q, register_9_q;

  Comparator comparator_1 (.a(register_2_q), .b({8{1'b0}}), .gt(comparator_1_gt));  // open: eq, lt
  Comparator comparator_2 (.a(register_3_q), .b({8{1'b0}}), .gt(comparator_2_gt));  // open: eq, lt
  Register register_1 (.D(multiplexer_2_out), .en(word_enable), .Q(register_1_q), .clk(Clock));  // open: clr
  BitSelector #(.width(32), .group(8)) bitselector_1 (.in(First), .out(bitselector_1_out), .sel(2'b11));
  BitSelector #(.width(32), .group(8)) bitselector_2 (.in(First), .out(bitselector_2_out), .sel(2'b10));
  assign bit_extender_1_out = {{3{1'b0}}, comparator_1_gt};  // Bit_Extender bit_extender_1
  assign bit_extender_2_out = {{3{1'b0}}, comparator_2_gt};  // Bit_Extender bit_extender_2
  assign controlled_buffer_1_out = A ? 8'h61 : 8'bz;  // Controlled_Buffer controlled_buffer_1
  assign controlled_buffer_1_out = B ? 8'h62 : 8'bz;  // Controlled_Buffer controlled_buffer_2
  assign controlled_buffer_1_out = C ? 8'h63 : 8'bz;  // Controlled_Buffer controlled_buffer_3
  assign controlled_buffer_1_out = D ? 8'h64 : 8'bz;  // Controlled_Buffer controlled_buffer_4
  assign controlled_buffer_1_out = E ? 8'h65 : 8'bz;  // Controlled_Buffer controlled_buffer_5
  assign controlled_buffer_1_out = F ? 8'h66 : 8'bz;  // Controlled_Buffer controlled_buffer_6
  assign controlled_buffer_1_out = G ? 8'h67 : 8'bz;  // Controlled_Buffer controlled_buffer_7
  assign controlled_buffer_1_out = H ? 8'h68 : 8'bz;  // Controlled_Buffer controlled_buffer_8
  assign controlled_buffer_1_out = I ? 8'h69 : 8'bz;  // Controlled_Buffer controlled_buffer_9
  assign controlled_buffer_1_out = J ? 8'h6a : 8'bz;  // Controlled_Buffer controlled_buffer_10
  assign controlled_buffer_1_out = K ? 8'h6b : 8'bz;  // Controlled_Buffer controlled_buffer_11
  assign controlled_buffer_1_out = L ? 8'h6c : 8'bz;  // Controlled_Buffer controlled_buffer_12
  assign controlled_buffer_1_out = M ? 8'h6d : 8'bz;  // Controlled_Buffer controlled_buffer_13
  assign controlled_buffer_1_out = N ? 8'h6e : 8'bz;  // Controlled_Buffer controlled_buffer_14
  assign controlled_buffer_1_out = O ? 8'h6f : 8'bz;  // Controlled_Buffer controlled_buffer_15
  assign controlled_buffer_1_out = P ? 8'h70 : 8'bz;  // Controlled_Buffer controlled_buffer_16
  assign controlled_buffer_1_out = Q ? 8'h71 : 8'bz;  // Controlled_Buffer controlled_buffer_17
  assign controlled_buffer_1_out = R ? 8'h72 : 8'bz;  // Controlled_Buffer controlled_buffer_18
  assign controlled_buffer_1_out = S ? 8'h73 : 8'bz;  // Controlled_Buffer controlled_buffer_19
  assign controlled_buffer_1_out = T ? 8'h74 : 8'bz;  // Controlled_Buffer controlled_buffer_20
  assign controlled_buffer_1_out = U ? 8'h75 : 8'bz;  // Controlled_Buffer controlled_buffer_21
  assign controlled_buffer_1_out = V ? 8'h76 : 8'bz;  // Controlled_Buffer controlled_buffer_22
  assign controlled_buffer_1_out = W ? 8'h77 : 8'bz;  // Controlled_Buffer controlled_buffer_23
  assign controlled_buffer_1_out = X ? 8'h78 : 8'bz;  // Controlled_Buffer controlled_buffer_24
  assign controlled_buffer_1_out = Y ? 8'h79 : 8'bz;  // Controlled_Buffer controlled_buffer_25
  assign controlled_buffer_1_out = Z ? 8'h7a : 8'bz;  // Controlled_Buffer controlled_buffer_26
  Register register_2 (.D(bitselector_1_out), .en(1'b1), .Q(register_2_q), .clk(Clock));  // open: clr
  Register register_3 (.D(bitselector_2_out), .en(1'b1), .Q(register_3_q), .clk(Clock));  // open: clr
  Adder #(.width(4)) adder_1 (.a(bit_extender_1_out), .b(bit_extender_2_out), .out(adder_1_out));  // open: cin, cout
  Comparator comparator_3 (.a(register_2_q), .b(register_1_q), .eq(comparator_3_eq));  // open: gt, lt
  Comparator comparator_4 (.a(register_3_q), .b(register_1_q), .eq(comparator_4_eq));  // open: gt, lt
  Comparator comparator_5 (.a(register_4_q), .b(register_1_q), .eq(comparator_5_eq));  // open: gt, lt
  Comparator comparator_6 (.a(register_5_q), .b(register_1_q), .eq(comparator_6_eq));  // open: gt, lt
  Comparator comparator_7 (.a(register_6_q), .b(register_1_q), .eq(comparator_7_eq));  // open: gt, lt
  Comparator comparator_8 (.a(register_7_q), .b(register_1_q), .eq(comparator_8_eq));  // open: gt, lt
  Comparator comparator_9 (.a(register_8_q), .b(register_1_q), .eq(comparator_9_eq));  // open: gt, lt
  Comparator comparator_10 (.a(register_9_q), .b(register_1_q), .eq(comparator_10_eq));  // open: gt, lt
  BitSelector #(.width(32), .group(8)) bitselector_3 (.in(First), .out(bitselector_3_out), .sel(2'b01));
  BitSelector #(.width(32), .group(8)) bitselector_4 (.in(First), .out(bitselector_4_out), .sel(2'b00));
  Adder #(.width(4)) adder_2 (.a(adder_1_out), .b(adder_4_out), .out(adder_2_out));  // open: cin, cout
  Register #(.width(5)) Number_of_word (
    .D(bit_extender_5_out), .en(1'b1), .Q(Number_of_word_q), .clk(Clock));  // open: clr
  Comparator comparator_11 (.a(register_5_q), .b({8{1'b0}}), .gt(comparator_11_gt));  // open: eq, lt
  Comparator comparator_12 (.a(register_4_q), .b({8{1'b0}}), .gt(comparator_12_gt));  // open: eq, lt
  or or_1 (eq, comparator_3_eq, comparator_4_eq, comparator_5_eq, comparator_6_eq, comparator_8_eq, comparator_7_eq, comparator_9_eq, comparator_10_eq);
  Register register_4 (.D(bitselector_3_out), .en(1'b1), .Q(register_4_q), .clk(Clock));  // open: clr
  Register register_5 (.D(bitselector_4_out), .en(1'b1), .Q(register_5_q), .clk(Clock));  // open: clr
  assign bit_extender_3_out = {{3{1'b0}}, comparator_11_gt};  // Bit_Extender bit_extender_3
  assign bit_extender_4_out = {{3{1'b0}}, comparator_12_gt};  // Bit_Extender bit_extender_4
  Adder #(.width(4)) adder_3 (.a(adder_5_out), .b(adder_2_out), .out(_7_segment_output));  // open: cin, cout
  assign bit_extender_5_out = {{1{1'b0}}, _7_segment_output};  // Bit_Extender bit_extender_5
  or or_2 (button, A, B, C, D, E, F, G, H, I, J, K, L, M, N, O, P, Q, R, S, T, U, V, W, X, Y, Z);
  Multiplexer #(.width(8), .enable("false")) multiplexer_1 (
    .in0(register_1_q), .in1(multiplexer_5_out), .out(multiplexer_1_out), .sel(tty_c_count));
  Adder #(.width(4)) adder_4 (.a(bit_extender_3_out), .b(bit_extender_4_out), .out(adder_4_out));  // open: cin, cout
  Multiplexer #(.width(8)) multiplexer_2 (
    .in0({8{1'b0}}), .in1(controlled_buffer_1_out), .out(multiplexer_2_out), .sel(word_mux_enable), .en(1'b1));
  Bit_Extender #(.out_width(7)) bit_extender_6 (.in(multiplexer_1_out), .out(tty_input));
  BitSelector #(.width(32), .group(8)) bitselector_5 (.in(Second), .out(bitselector_5_out), .sel(2'b11));
  BitSelector #(.width(32), .group(8)) bitselector_6 (.in(Second), .out(bitselector_6_out), .sel(2'b10));
  Comparator comparator_13 (.a(register_7_q), .b({8{1'b0}}), .gt(comparator_13_gt));  // open: eq, lt
  Comparator comparator_14 (.a(register_6_q), .b({8{1'b0}}), .gt(comparator_14_gt));  // open: eq, lt
  Adder #(.width(4)) adder_5 (.a(adder_8_out), .b(adder_10_out), .out(adder_5_out));  // open: cin, cout
  Register register_6 (.D(bitselector_5_out), .en(1'b1), .Q(register_6_q), .clk(Clock));  // open: clr
  Register register_7 (.D(bitselector_6_out), .en(1'b1), .Q(register_7_q), .clk(Clock));  // open: clr
  assign bit_extender_7_out = {{3{1'b0}}, comparator_13_gt};  // Bit_Extender bit_extender_7
  assign bit_extender_8_out = {{3{1'b0}}, comparator_14_gt};  // Bit_Extender bit_extender_8
  Adder #(.width(5)) adder_6 (.a(c_miss_q), .b(5'b00001), .out(adder_6_out));  // open: cin, cout
  Adder #(.width(5)) adder_7 (.a(bulunan_q), .b(5'b00001), .out(adder_7_out));  // open: cin, cout
  Multiplexer #(.width(5), .enable("false")) multiplexer_3 (
    .in0({5{1'b0}}), .in1(adder_6_out), .out(multiplexer_3_out), .sel(miss_mux));
  Counter #(.width(5), .max('h1f)) counter_1 (
    .count(c_count), .Q(counter_1_q), .clk(Clock), .clr(clear));  // open: load, D, carry
  BitSelector #(.width(32), .group(8)) bitselector_7 (.in(Second), .out(bitselector_7_out), .sel(2'b01));
  BitSelector #(.width(32), .group(8)) bitselector_8 (.in(Second), .out(bitselector_8_out), .sel(2'b00));
  Adder #(.width(4)) adder_8 (.a(bit_extender_7_out), .b(bit_extender_8_out), .out(adder_8_out));  // open: cin, cout
  Register #(.width(5)) c_miss (.D(multiplexer_3_out), .en(e_miss), .Q(c_miss_q), .clk(Clock));  // open: clr
  Register register_8 (.D(bitselector_7_out), .en(1'b1), .Q(register_8_q), .clk(Clock));  // open: clr
  Multiplexer #(.width(5), .enable("false")) multiplexer_4 (
    .in0({5{1'b0}}), .in1(adder_7_out), .out(multiplexer_4_out), .sel(bulunan_mux));
  Adder #(.width(5)) adder_9 (.a(5'b01001), .b(5'b00001), .out(adder_9_out));  // open: cin, cout
  Multiplexer #(.select(4), .width(8), .enable("false")) multiplexer_5 (
    .in1(register_9_q), .in2(register_8_q), .in3(register_7_q), .in4(register_6_q), .in5(register_5_q),
    .in6(register_4_q), .in7(register_3_q), .in8(register_2_q), .out(multiplexer_5_out), .sel(counter_2_q));  // open: in0, in9, in10, in11, in12, in13, in14, in15
  Counter #(.width(4), .max('hf)) counter_2 (
    .load(1'b1), .D(_7_segment_output), .count(tty_c_count), .Q(counter_2_q), .clk(Clock));  // open: carry, clr
  Register register_9 (.D(bitselector_8_out), .en(1'b1), .Q(register_9_q), .clk(Clock));  // open: clr
  Comparator comparator_15 (.a(register_8_q), .b({8{1'b0}}), .gt(comparator_15_gt));  // open: eq, lt
  Comparator comparator_16 (.a(register_9_q), .b({8{1'b0}}), .gt(comparator_16_gt));  // open: eq, lt
  Register #(.width(5)) bulunan (.D(multiplexer_4_out), .en(e_bulunan), .Q(bulunan_q), .clk(Clock));  // open: clr
  Comparator #(.width(5)) comparator_17 (.a(c_miss_q), .b(adder_9_out), .eq(miss_eq_10), .lt(miss_lt_10));  // open: gt
  Comparator #(.width(5)) comparator_18 (.a(counter_1_q), .b({5{1'b0}}), .gt(led1));  // open: eq, lt
  Comparator #(.width(5)) comparator_19 (.a(counter_1_q), .b(5'b00001), .gt(led2));  // open: eq, lt
  Comparator #(.width(5)) comparator_20 (.a(counter_1_q), .b(5'b00010), .gt(led3));  // open: eq, lt
  Comparator #(.width(5)) comparator_21 (.a(counter_1_q), .b(5'b00011), .gt(led4));  // open: eq, lt
  Comparator #(.width(5)) comparator_22 (.a(counter_1_q), .b(5'b00100), .gt(led5));  // open: eq, lt
  Comparator #(.width(5)) comparator_23 (.a(counter_1_q), .b(5'b00101), .gt(led6));  // open: eq, lt
  Comparator #(.width(5)) comparator_24 (.a(counter_1_q), .b(5'b00110), .gt(led7));  // open: eq, lt
  Comparator #(.width(5)) comparator_25 (.a(counter_1_q), .b(5'b00111), .gt(led8));  // open: eq, lt
  Comparator #(.width(5)) comparator_26 (.a(counter_1_q), .b(5'b01000), .gt(led9));  // open: eq, lt
  Comparator #(.width(5)) comparator_27 (.a(counter_1_q), .b(5'b01001), .gt(led10));  // open: eq, lt
  assign bit_extender_9_out = {{3{1'b0}}, comparator_15_gt};  // Bit_Extender bit_extender_9
  assign bit_extender_10_out = {{3{1'b0}}, comparator_16_gt};  // Bit_Extender bit_extender_10
  Comparator #(.width(4)) comparator_28 (.a(counter_2_q), .b(4'b0010), .lt(print));  // open: gt, eq
  Adder #(.width(4)) adder_10 (.a(bit_extender_9_out), .b(bit_extender_10_out), .out(adder_10_out));  // open: cin, cout
  Comparator #(.width(5)) comparator_29 (
    .a(bulunan_q), .b(Number_of_word_q), .eq(eq_bulunan), .lt(lt_bulunan));  // open: gt

  assign lose_c = led10;
endmodule
