// Logisim project Circuit of Fsm.circ as structural Verilog: 1 circuit, main circuit main
module main (
);

  wire and_1_out, and_2_out, and_3_out, and_4_out, and_5_out, and_6_out, and_7_out, and_8_out, and_9_out,
       and_10_out, and_11_out, and_12_out, and_13_out, and_14_out, and_15_out, and_16_out, and_17_out,
       and_18_out, and_19_out, and_20_out, and_21_out, and_22_out, and_23_out, and_24_out, and_25_out,
       and_26_out, and_27_out, and_28_out, and_29_out, and_30_out, and_31_out, and_32_out, and_33_out,
       and_34_out, and_35_out, and_36_out, and_37_out, and_38_out, and_39_out, and_40_out, and_41_out,
       and_42_out, and_43_out, and_44_out, and_45_out, and_46_out, and_47_out, and_48_out, and_49_out,
       and_50_out, and_51_out, and_52_out, and_54_out, and_55_out, and_56_out, button_1_out, button_2_out,
       button_3_out, clock_1_out, clock_2_out, clock_3_out, not_1_out, not_2_out, not_3_out, not_4_out,
       not_5_out, not_6_out, not_7_out, not_8_out, not_9_out, not_10_out, not_11_out, not_12_out, not_13_out,
       not_14_out, not_15_out, not_16_out, not_17_out, not_18_out, not_19_out, not_20_out, not_21_out,
       not_22_out, not_23_out, not_24_out, not_25_out, not_26_out, not_27_out, not_28_out, not_29_out,
       not_30_out, not_31_out, not_32_out, not_33_out, not_34_out, not_35_out, not_36_out, not_37_out,
       not_38_out, not_39_out, not_40_out, not_41_out, not_42_out, not_43_out, not_44_out, not_45_out,
       not_46_out, not_47_out, not_48_out, not_49_out, not_50_out, not_51_out, not_52_out, not_53_out,
       not_54_out, not_55_out, not_56_out, not_57_out, not_58_out, not_59_out, not_60_out, not_61_out,
       not_62_out, not_63_out, not_64_out, not_65_out, not_66_out, not_67_out, not_68_out, not_69_out,
       not_70_out, not_71_out, not_72_out, not_73_out, not_74_out, not_75_out, not_76_out, not_77_out,
       not_78_out, not_79_out, not_80_out, not_81_out, not_82_out, not_83_out, not_84_out, not_85_out,
       not_86_out, not_87_out, not_88_out, not_89_out, not_90_out, not_91_out, not_92_out, not_93_out,
       not_94_out, not_95_out, not_96_out, not_97_out, not_98_out, not_99_out, not_100_out, not_101_out,
       not_102_out, not_103_out, not_104_out, not_105_out, not_106_out, not_107_out, not_108_out,
       not_109_out, not_110_out, not_111_out, not_112_out, not_113_out, not_114_out, not_115_out, or_4_out,
       or_5_out, or_6_out, or_7_out, or_8_out, or_9_out, or_10_out, or_12_out;
  wire [1:0] and_53_out, and_57_out, State_2_q, State_3_q;
  wire [2:0] or_3_out, State_q;

  Button button_1 (.out(button_1_out));
  Button button_2 (.out(button_2_out));
  Button button_3 (.out(button_3_out));
  LED led_1 (.in(or_4_out));
  LED led_2 (.in(or_5_out));
  LED led_3 (.in(or_6_out));
  LED led_4 (.in(or_7_out));
  LED led_5 (.in(or_8_out));
  LED led_6 (.in(or_9_out));
  LED led_7 (.in(or_10_out));
  LED led_8 (.in(or_12_out));
  Clock clock_1 (.out(clock_1_out));
  Register #(.width(3)) State (.D(or_3_out), .en(1'b1), .Q(State_q), .clk(clock_1_out), .clr(button_2_out));
  not not_1 (not_1_out, and_50_out);
  not not_2 (not_2_out, and_50_out);
  not not_3 (not_3_out, State_q[2]);
  not not_4 (not_4_out, State_q[1]);
  not not_5 (not_5_out, and_50_out);
  not not_6 (not_6_out, State_q[0]);
  and and_1 (and_1_out, State_q[2], not_6_out, not_7_out);
  not not_7 (not_7_out, and_54_out);
  not not_8 (not_8_out, and_54_out);
  and and_2 (and_2_out, State_q[2], not_8_out, not_9_out);
  not not_9 (not_9_out, and_50_out);
  and and_3 (and_3_out, State_q[2], and_54_out, and_50_out);
  and and_4 (and_4_out, State_q[2], State_q[1], not_10_out);
  not not_10 (not_10_out, State_q[0]);
  not not_11 (not_11_out, State_q[0]);
  and and_5 (and_5_out, State_q[1], not_11_out, not_12_out, and_50_out);
  not not_12 (not_12_out, and_54_out);
  not not_13 (not_13_out, State_q[1]);
  and and_6 (and_6_out, State_q[2], not_13_out, State_q[0], not_14_out);
  not not_14 (not_14_out, and_50_out);
  not not_15 (not_15_out, State_q[2]);
  and and_7 (and_7_out, not_15_out, State_q[1], State_q[0], and_54_out, not_16_out);
  not not_16 (not_16_out, and_50_out);
  and and_8 (and_8_out, State_q[1], not_17_out, not_18_out);
  not not_17 (not_17_out, and_54_out);
  not not_18 (not_18_out, and_50_out);
  and and_9 (and_9_out, State_q[1], and_54_out, and_50_out);
  not not_19 (not_19_out, State_q[0]);
  and and_10 (and_10_out, State_q[2], not_19_out, and_50_out);
  not not_20 (not_20_out, State_q[1]);
  not not_21 (not_21_out, State_q[0]);
  and and_11 (and_11_out, not_20_out, not_21_out, not_22_out, and_50_out);
  not not_22 (not_22_out, and_54_out);
  not not_23 (not_23_out, State_q[1]);
  and and_12 (and_12_out, not_23_out, State_q[0], and_54_out, not_24_out);
  not not_24 (not_24_out, and_50_out);
  not not_25 (not_25_out, State_q[1]);
  and and_13 (and_13_out, State_q[2], not_25_out, not_26_out, and_50_out);
  not not_26 (not_26_out, and_54_out);
  not not_27 (not_27_out, and_54_out);
  and and_14 (and_14_out, State_q[0], not_27_out, not_1_out);
  and and_15 (and_15_out, State_q[0], and_54_out, and_50_out);
  not not_28 (not_28_out, State_q[2]);
  and and_16 (and_16_out, not_28_out, State_q[1], State_q[0]);
  not not_29 (not_29_out, State_q[1]);
  and and_17 (and_17_out, State_q[2], not_29_out, State_q[0]);
  not not_30 (not_30_out, State_q[2]);
  and and_18 (and_18_out, not_30_out, not_31_out, and_54_out, not_32_out);
  not not_31 (not_31_out, State_q[1]);
  not not_32 (not_32_out, and_50_out);
  and and_19 (and_19_out, State_q[2], State_q[1], not_33_out, not_34_out, and_50_out);
  not not_33 (not_33_out, State_q[0]);
  not not_34 (not_34_out, and_54_out);
  not not_35 (not_35_out, State_q[1]);
  and and_20 (and_20_out, State_q[2], not_35_out, State_q[0], not_36_out, not_2_out);
  not not_36 (not_36_out, and_54_out);
  not not_37 (not_37_out, State_q[1]);
  and and_21 (and_21_out, State_q[2], not_37_out, State_q[0], not_38_out, not_39_out);
  not not_38 (not_38_out, and_54_out);
  not not_39 (not_39_out, and_50_out);
  and and_22 (and_22_out, not_3_out, not_4_out, State_q[0], and_54_out, not_5_out);
  not not_40 (not_40_out, State_q[2]);
  and and_23 (and_23_out, not_40_out, State_q[1], State_q[0], not_41_out, not_42_out);
  not not_41 (not_41_out, and_54_out);
  not not_42 (not_42_out, and_50_out);
  not not_43 (not_43_out, State_q[2]);
  and and_24 (and_24_out, not_43_out, State_q[1], State_q[0], and_54_out, and_50_out);
  not not_44 (not_44_out, State_q[1]);
  and and_25 (and_25_out, State_q[2], not_44_out, State_q[0], not_45_out, and_50_out);
  not not_45 (not_45_out, and_54_out);
  not not_46 (not_46_out, State_q[2]);
  not not_47 (not_47_out, State_q[1]);
  not not_48 (not_48_out, State_q[0]);
  and and_26 (and_26_out, not_46_out, not_47_out, not_48_out, and_54_out, not_49_out);
  not not_49 (not_49_out, and_50_out);
  not not_50 (not_50_out, State_q[2]);
  not not_51 (not_51_out, State_q[1]);
  and and_27 (and_27_out, not_50_out, not_51_out, State_q[0], not_52_out, not_53_out);
  not not_52 (not_52_out, and_54_out);
  not not_53 (not_53_out, and_50_out);
  not not_54 (not_54_out, State_q[2]);
  not not_55 (not_55_out, State_q[1]);
  and and_28 (and_28_out, not_54_out, not_55_out, State_q[0], and_54_out, and_50_out);
  not not_56 (not_56_out, State_q[2]);
  and and_29 (and_29_out, not_56_out, State_q[1], State_q[0], not_57_out, and_50_out);
  not not_57 (not_57_out, and_54_out);
  not not_58 (not_58_out, State_q[2]);
  not not_59 (not_59_out, State_q[1]);
  and and_30 (and_30_out, not_58_out, not_59_out, not_60_out, not_61_out, not_62_out);
  not not_60 (not_60_out, State_q[0]);
  not not_61 (not_61_out, and_54_out);
  not not_62 (not_62_out, and_50_out);
  not not_63 (not_63_out, State_q[2]);
  not not_64 (not_64_out, State_q[1]);
  not not_65 (not_65_out, State_q[0]);
  and and_31 (and_31_out, not_63_out, not_64_out, not_65_out, and_54_out, and_50_out);
  not not_66 (not_66_out, State_q[2]);
  not not_67 (not_67_out, State_q[1]);
  and and_32 (and_32_out, not_66_out, not_67_out, State_q[0], not_68_out, and_50_out);
  not not_68 (not_68_out, and_54_out);
  not not_69 (not_69_out, State_q[2]);
  not not_70 (not_70_out, State_q[0]);
  and and_33 (and_33_out, not_69_out, State_q[1], not_70_out, and_54_out, not_71_out);
  not not_71 (not_71_out, and_50_out);
  and and_34 (and_34_out, State_q[2], State_q[1], State_q[0], not_72_out, and_50_out);
  not not_72 (not_72_out, and_54_out);
  and and_35 (and_35_out, State_q[2], State_q[1], State_q[0], and_54_out, not_73_out);
  not not_73 (not_73_out, and_50_out);
  not not_74 (not_74_out, State_q[2]);
  not not_75 (not_75_out, State_q[0]);
  and and_36 (and_36_out, not_74_out, not_75_out, not_76_out, and_50_out);
  not not_76 (not_76_out, and_54_out);
  not not_77 (not_77_out, State_q[2]);
  and and_37 (and_37_out, not_77_out, State_q[1], not_78_out, not_79_out);
  not not_78 (not_78_out, State_q[0]);
  not not_79 (not_79_out, and_54_out);
  not not_80 (not_80_out, State_q[2]);
  and and_38 (and_38_out, not_80_out, State_q[1], not_81_out, and_50_out);
  not not_81 (not_81_out, State_q[0]);
  not not_82 (not_82_out, State_q[1]);
  and and_39 (and_39_out, State_q[2], not_82_out, not_83_out, and_54_out, not_84_out);
  not not_83 (not_83_out, State_q[0]);
  not not_84 (not_84_out, and_50_out);
  not not_85 (not_85_out, State_q[1]);
  and and_40 (and_40_out, State_q[2], not_85_out, not_86_out, not_87_out, not_88_out);
  not not_86 (not_86_out, State_q[0]);
  not not_87 (not_87_out, and_54_out);
  not not_88 (not_88_out, and_50_out);
  not not_89 (not_89_out, State_q[1]);
  and and_41 (and_41_out, State_q[2], not_89_out, not_90_out, and_54_out, and_50_out);
  not not_90 (not_90_out, State_q[0]);
  and and_42 (and_42_out, State_q[2], State_q[1], not_91_out, and_54_out, not_92_out);
  not not_91 (not_91_out, State_q[0]);
  not not_92 (not_92_out, and_50_out);
  not not_93 (not_93_out, State_q[1]);
  and and_43 (and_43_out, State_q[2], not_93_out, not_94_out, not_95_out, and_50_out);
  not not_94 (not_94_out, State_q[0]);
  not not_95 (not_95_out, and_54_out);
  and and_44 (and_44_out, State_q[2], State_q[1], not_96_out, not_97_out, not_98_out);
  not not_96 (not_96_out, State_q[0]);
  not not_97 (not_97_out, and_54_out);
  not not_98 (not_98_out, and_50_out);
  and and_45 (and_45_out, State_q[2], State_q[1], not_99_out, and_54_out, and_50_out);
  not not_99 (not_99_out, State_q[0]);
  not not_100 (not_100_out, State_q[1]);
  and and_46 (and_46_out, State_q[2], not_100_out, State_q[0], and_54_out, not_101_out);
  not not_101 (not_101_out, and_50_out);
  and and_47 (and_47_out, State_q[2], State_q[1], not_102_out, not_103_out, and_50_out);
  not not_102 (not_102_out, State_q[0]);
  not not_103 (not_103_out, and_54_out);
  and and_48 (and_48_out, State_q[2], State_q[1], State_q[0], not_104_out, not_105_out);
  not not_104 (not_104_out, and_54_out);
  not not_105 (not_105_out, and_50_out);
  and and_49 (and_49_out, State_q[2], State_q[1], State_q[0], and_54_out, and_50_out);
  or or_1 (or_3_out[2], and_1_out, and_6_out, and_2_out, and_3_out, and_4_out, and_5_out, and_7_out);
  or or_2 (or_3_out[1], and_8_out, and_9_out, and_10_out, and_11_out, and_12_out, and_13_out);
  or or_3 (or_3_out[0], and_14_out, and_15_out, and_16_out, and_17_out, and_18_out, and_19_out);
  or or_4 (or_4_out, and_7_out, and_20_out, and_21_out);
  or or_5 (or_5_out, and_22_out, and_23_out, and_24_out, and_25_out);
  or or_6 (or_6_out, and_26_out, and_27_out, and_28_out, and_29_out);
  or or_7 (or_7_out, and_30_out, and_31_out, and_32_out, and_33_out, and_34_out, and_35_out);
  or or_8 (or_8_out, and_36_out, and_37_out, and_38_out, and_39_out);
  or or_9 (or_9_out, and_40_out, and_41_out, and_42_out);
  or or_10 (or_10_out, and_43_out, and_44_out, and_45_out);
  // OR_Gate or_11 has open pins: in0=and_46_out, in1=and_47_out, in2=and_48_out, in3=and_49_out, out=open
  or or_12 (or_12_out, or_4_out, or_10_out);
  Clock clock_2 (.out(clock_2_out));
  Clock clock_3 (.out(clock_3_out));
  Register #(.width(2)) State_2 (.D(and_57_out), .en(1'b1), .Q(State_2_q), .clk(clock_2_out));  // open: clr
  Register #(.width(2)) State_3 (.D(and_53_out), .en(1'b1), .Q(State_3_q), .clk(clock_3_out));  // open: clr
  not not_106 (not_106_out, State_3_q[1]);
  not not_107 (not_107_out, State_3_q[1]);
  not not_108 (not_108_out, State_3_q[0]);
  not not_109 (not_109_out, State_3_q[0]);
  not not_110 (not_110_out, State_3_q[1]);
  not not_111 (not_111_out, State_2_q[1]);
  not not_112 (not_112_out, State_2_q[1]);
  not not_113 (not_113_out, State_2_q[0]);
  not not_114 (not_114_out, State_2_q[0]);
  not not_115 (not_115_out, State_2_q[1]);
  and and_50 (and_50_out, not_106_out, State_3_q[0]);
  and and_51 (and_51_out, button_3_out, not_107_out, State_3_q[0]);
  and and_52 (and_52_out, button_3_out, not_108_out, State_3_q[1]);
  and and_53 (and_53_out[0], button_3_out, not_109_out, not_110_out);
  and and_54 (and_54_out, not_111_out, State_2_q[0]);
  and and_55 (and_55_out, button_1_out, not_112_out, State_2_q[0]);
  and and_56 (and_56_out, button_1_out, not_113_out, State_2_q[1]);
  and and_57 (and_57_out[0], button_1_out, not_114_out, not_115_out);
  or or_13 (and_57_out[1], and_55_out, and_56_out);
  or or_14 (and_53_out[1], and_51_out, and_52_out);

  // Notes on the sheet:
  //   BUTTON 1
  //   RESET
  //   BUTTON 2
  //   Led 1
  //   Led 2
  //   Led 3
  //   Led 4
  //   Led 5
  //   Led 6
  //   Led 7
  //   WİN!!
  //   s1
  //   s2
  //   s0
  //   n1
  //   n0
  //     n2
  //   n0
  //   n0
endmodule
