// Logisim project Test.circ as structural Verilog: 1 circuit, main circuit main
module main (
  input  [15:0] A,
  input  [15:0] B,
  output [2:0] States,
  output [31:0] Result
);

  wire clock_1_out, main_1_c_count, main_1_c_load, main_1_l_a, main_1_l_mult, main_1_s_a, main_1_s_mult,
       main_2_eq, main_2_gt, main_2_lt, Start_out;

  Button Start (.out(Start_out));
  Clock clock_1 (.out(clock_1_out));
  control_unit_main main_1 (
    .lt(main_2_lt), .start(Start_out), .gt(main_2_gt), .eq(main_2_eq), .Clock(clock_1_out),
    .L_mult(main_1_l_mult), .S_mult(main_1_s_mult), .L_a(main_1_l_a), .C_load(main_1_c_load),
    .S_a(main_1_s_a), .C_count(main_1_c_count), .state(States));
  datapath_main main_2 (
    .Input_b(B), .L_mult(main_1_l_mult), .Input_a(A), .L_a(main_1_l_a), .Clock(clock_1_out),
    .S_a(main_1_s_a), .C_load(main_1_c_load), .C_count(main_1_c_count), .S_mult(main_1_s_mult),
    .gt(main_2_gt), .eq(main_2_eq), .lt(main_2_lt), .Mult(Result));  // open: _0_Register, _0_Register_2
endmodule
