// Logisim project 171044063_erdi_bayir_lab2.circ as structural Verilog: 1 circuit, main circuit main
module main (
  input  s1,
  input  s2,
  input  s3,
  input  s4,
  input  s5,
  output Output
);

  wire and_1_out, and_2_out, and_3_out, and_4_out, and_5_out, and_6_out, and_7_out, and_8_out, and_9_out,
       and_10_out, and_11_out, and_12_out, and_13_out, and_14_out, and_15_out, not_1_out, not_2_out,
       not_3_out, not_4_out, not_5_out, not_6_out, not_7_out, not_8_out, not_9_out, not_10_out, not_11_out,
       not_12_out, or_1_out, or_2_out;

  not not_1 (not_1_out, s2);
  not not_2 (not_2_out, s1);
  not not_3 (not_3_out, s2);
  not not_4 (not_4_out, s4);
  not not_5 (not_5_out, s2);
  not not_6 (not_6_out, s3);
  not not_7 (not_7_out, s4);
  not not_8 (not_8_out, s5);
  not not_9 (not_9_out, s3);
  not not_10 (not_10_out, s4);
  not not_11 (not_11_out, s1);
  not not_12 (not_12_out, s5);
  and and_1 (and_1_out, not_1_out, s3);
  and and_2 (and_2_out, s4, s5);
  and and_3 (and_3_out, not_2_out, not_3_out, s3);
  and and_4 (and_4_out, not_4_out, s5);
  and and_5 (and_5_out, s1, not_5_out, not_6_out);
  and and_6 (and_6_out, not_7_out, not_8_out);
  and and_7 (and_7_out, s1, s2, not_9_out);
  and and_8 (and_8_out, not_10_out, s5);
  and and_9 (and_9_out, not_11_out, s2, s3);
  and and_10 (and_10_out, s4, not_12_out);
  and and_11 (and_11_out, and_1_out, and_2_out);
  and and_12 (and_12_out, and_3_out, and_4_out);
  and and_13 (and_13_out, and_5_out, and_6_out);
  and and_14 (and_14_out, and_7_out, and_8_out);
  and and_15 (and_15_out, and_9_out, and_10_out);
  or or_1 (or_1_out, and_11_out, and_12_out);
  or or_2 (or_2_out, and_13_out, and_14_out, and_15_out);
  or or_3 (Output, or_1_out, or_2_out);
endmodule
