// Logisim project erdi_bayir_171044063_lab3.circ as structural Verilog: 1 circuit, main circuit main
module main (
  input  A,
  input  B,
  output X,
  output [1:0] out_4
);

  wire and_1_out, and_2_out, and_3_out, and_4_out, and_5_out, and_6_out, and_7_out, clock_1_out, not_1_out,
       not_2_out, not_3_out, not_4_out, not_5_out, not_6_out, not_7_out;
  wire [1:0] or_1_out;

  Clock clock_1 (.out(clock_1_out));
  Register #(.width(2)) register_1 (.D(or_1_out), .en(1'b1), .Q(out_4), .clk(clock_1_out));  // open: clr
  not not_1 (not_1_out, A);
  not not_2 (not_2_out, out_4[1]);
  not not_3 (not_3_out, B);
  not not_4 (not_4_out, A);
  not not_5 (not_5_out, out_4[0]);
  not not_6 (not_6_out, A);
  not not_7 (not_7_out, out_4[1]);
  and and_1 (and_1_out, out_4[1], out_4[0], A, B);
  and and_2 (and_2_out, out_4[1], not_1_out, B);
  and and_3 (and_3_out, not_2_out, A, not_3_out);
  and and_4 (and_4_out, out_4[1], out_4[0], not_4_out, B);
  and and_5 (and_5_out, out_4[1], A, B);
  and and_6 (and_6_out, out_4[1], not_5_out, not_6_out);
  and and_7 (and_7_out, not_7_out, out_4[0], A);
  or or_1 (or_1_out[0], and_1_out, and_2_out, and_3_out);
  or or_2 (or_1_out[1], and_4_out, and_5_out, and_6_out, and_7_out);

  assign X = out_4[1];
endmodule
