// Logisim project erdi_bayir_171044063_lab4.circ as structural Verilog: 1 circuit, main circuit main
module main (
  input  Req,
  input  P3s,
  input  P7s,
  input  P37s,
  output [1:0] out_5
);

  wire and_1_out, and_2_out, and_3_out, and_4_out, and_5_out, and_6_out, and_7_out, clock_1_out, not_1_out,
       not_2_out, not_3_out, not_4_out, not_5_out, not_6_out, not_7_out, not_8_out, not_9_out, not_10_out,
       not_11_out;
  wire [1:0] or_2_out;

  Clock clock_1 (.out(clock_1_out));
  Register #(.width(2)) register_1 (.D(or_2_out), .en(1'b1), .Q(out_5), .clk(clock_1_out));  // open: clr
  not not_1 (not_1_out, out_5[1]);
  not not_2 (not_2_out, P7s);
  not not_3 (not_3_out, out_5[1]);
  not not_4 (not_4_out, out_5[0]);
  not not_5 (not_5_out, out_5[0]);
  not not_6 (not_6_out, P37s);
  not not_7 (not_7_out, out_5[1]);
  not not_8 (not_8_out, out_5[1]);
  not not_9 (not_9_out, out_5[0]);
  not not_10 (not_10_out, out_5[1]);
  not not_11 (not_11_out, out_5[0]);
  and and_1 (and_1_out, not_1_out, out_5[0], not_2_out);
  and and_2 (and_2_out, not_3_out, not_4_out, Req, P3s);
  and and_3 (and_3_out, out_5[1], not_5_out, not_6_out);
  and and_4 (and_4_out, not_7_out, out_5[0], P7s);
  and and_5 (and_5_out, not_8_out, not_9_out);
  and and_6 (and_6_out, not_10_out, out_5[0]);
  and and_7 (and_7_out, out_5[1], not_11_out);
  or or_1 (or_2_out[1], and_3_out, and_4_out);
  or or_2 (or_2_out[0], and_1_out, and_2_out);
  LED RED (.in(and_5_out));
  LED ORANGE (.in(and_6_out));
  LED GREEN (.in(and_7_out));
  LED RESET (.in(and_5_out));

  // Notes on the sheet:
  //   n1
  //   n0
endmodule
