// Logisim project datapath.circ as structural Verilog: 1 circuit, main circuit main
module main (
  input  CLOCK,
  input  Reset,
  output P3s,
  output P7s,
  output P37_s
);

  wire comparator_1_eq, comparator_1_gt, comparator_2_eq, comparator_2_gt, comparator_3_eq, comparator_3_gt;
  wire [6:0] counter_1_q;

  Counter #(.width(7), .max('h7f)) counter_1 (
    .load(1'b0), .count(1'b1), .Q(counter_1_q), .clk(CLOCK), .clr(Reset));  // open: D, carry
  Comparator #(.width(7)) comparator_1 (
    .a(counter_1_q), .b(7'b0000010), .gt(comparator_1_gt), .eq(comparator_1_eq));  // open: lt
  Comparator #(.width(7)) comparator_2 (
    .a(counter_1_q), .b(7'b0000110), .gt(comparator_2_gt), .eq(comparator_2_eq));  // open: lt
  Comparator #(.width(7)) comparator_3 (
    .a(counter_1_q), .b(7'b0100100), .gt(comparator_3_gt), .eq(comparator_3_eq));  // open: lt
  or or_1 (P3s, comparator_1_gt, comparator_1_eq);
  or or_2 (P7s, comparator_2_gt, comparator_2_eq);
  or or_3 (P37_s, comparator_3_gt, comparator_3_eq);
endmodule
