// Logisim project erdi_bayir_171044063_lab4.circ as structural Verilog: 1 circuit, main circuit main
module main (
  input  Req,
  input  P3s,
  input  P7s,
  input  P37s,
  input  CLOCK,
  output RED,
  output ORANGE,
  output GREEN,
  output Reset,
  output [1:0] STATE
);

  wire and_3_out, and_4_out, and_5_out, and_6_out, and_7_out, and_8_out, and_9_out, not_1_out, not_2_out,
       not_3_out, not_4_out, not_5_out, not_6_out, not_7_out, not_8_out, not_9_out, not_10_out, not_11_out,
       not_12_out;
  wire [1:0] or_1_out;

  Register #(.width(2)) register_1 (.D(or_1_out), .en(1'b1), .Q(STATE), .clk(CLOCK));  // open: clr
  not not_1 (not_1_out, STATE[0]);
  not not_2 (not_2_out, STATE[1]);
  not not_3 (not_3_out, STATE[0]);
  not not_4 (not_4_out, P37s);
  not not_5 (not_5_out, STATE[0]);
  not not_6 (not_6_out, STATE[1]);
  not not_7 (not_7_out, P3s);
  not not_8 (not_8_out, STATE[1]);
  not not_9 (not_9_out, STATE[0]);
  not not_10 (not_10_out, STATE[1]);
  not not_11 (not_11_out, P37s);
  not not_12 (not_12_out, STATE[0]);
  and and_1 (ORANGE, STATE[1], not_1_out);
  and and_2 (Reset, not_2_out, not_3_out);
  and and_3 (and_3_out, STATE[1], STATE[0], not_4_out);
  and and_4 (and_4_out, STATE[1], not_5_out, P7s);
  and and_5 (and_5_out, not_6_out, STATE[0], not_7_out);
  and and_6 (and_6_out, not_8_out, not_9_out, Req);
  and and_7 (and_7_out, not_10_out, STATE[0], P3s);
  and and_8 (and_8_out, STATE[1], STATE[0], not_11_out);
  and and_9 (and_9_out, STATE[1], not_12_out);
  or or_1 (or_1_out[0], and_3_out, and_4_out, and_5_out, and_6_out);
  and and_10 (GREEN, STATE[1], STATE[0]);
  or or_2 (or_1_out[1], and_7_out, and_8_out, and_9_out);
  not not_13 (RED, STATE[1]);
endmodule
