// Logisim project test.circ as structural Verilog: 1 circuit, main circuit main
module main (
  input  REQ,
  output [1:0] out_2
);

  wire clock_1_out, main_1_green, main_1_orange, main_1_red, main_1_reset, main_2_p3s, main_2_p7s,
       main_2_p37_s;

  Clock clock_1 (.out(clock_1_out));
  erdi_bayir_171044063_lab4_main main_1 (
    .Req(REQ), .P3s(main_2_p3s), .P7s(main_2_p7s), .P37s(main_2_p37_s), .CLOCK(clock_1_out),
    .RED(main_1_red), .ORANGE(main_1_orange), .GREEN(main_1_green), .Reset(main_1_reset), .STATE(out_2));
  datapath_main main_2 (
    .CLOCK(clock_1_out), .Reset(main_1_reset), .P3s(main_2_p3s), .P7s(main_2_p7s), .P37_s(main_2_p37_s));
  LED RED (.in(main_1_red));
  LED ORANGE (.in(main_1_orange));
  LED GREEN (.in(main_1_green));
  LED RESET (.in(main_1_reset));
endmodule
