// Logisim project control_unit.circ as structural Verilog: 1 circuit, main circuit main
module main (
  input  eol,
  input  gt,
  input  goi,
  input  Clock,
  output x_enable,
  output y_enable,
  output z_enable,
  output diff_enable,
  output diff2_enable,
  output z_mux,
  output diff_mux,
  output [2:0] STATE
);

  wire and_1_out, and_2_out, and_3_out, and_5_out, and_6_out, and_7_out, and_8_out, and_9_out, and_10_out,
       and_11_out, and_12_out, not_1_out, not_2_out, not_3_out, not_4_out, not_5_out, not_6_out, not_7_out,
       not_8_out, not_9_out, not_10_out, not_11_out, not_12_out, not_13_out, not_14_out, not_15_out,
       not_16_out, not_17_out, not_18_out, not_19_out, not_20_out, not_21_out, not_22_out, not_23_out,
       not_24_out;
  wire [2:0] or_3_out;

  Register #(.width(3)) register_1 (.D(or_3_out), .en(1'b1), .Q(STATE), .clk(Clock));  // open: clr
  not not_1 (not_1_out, STATE[1]);
  not not_2 (not_2_out, STATE[2]);
  not not_3 (not_3_out, STATE[0]);
  not not_4 (not_4_out, STATE[1]);
  not not_5 (not_5_out, STATE[2]);
  not not_6 (not_6_out, STATE[1]);
  not not_7 (not_7_out, STATE[1]);
  not not_8 (not_8_out, STATE[0]);
  not not_9 (not_9_out, eol);
  not not_10 (not_10_out, STATE[2]);
  not not_11 (not_11_out, STATE[0]);
  not not_12 (not_12_out, STATE[2]);
  not not_13 (not_13_out, STATE[1]);
  not not_14 (not_14_out, STATE[0]);
  not not_15 (not_15_out, STATE[2]);
  not not_16 (not_16_out, STATE[0]);
  not not_17 (not_17_out, STATE[2]);
  not not_18 (not_18_out, STATE[1]);
  not not_19 (not_19_out, STATE[1]);
  not not_20 (not_20_out, STATE[1]);
  not not_21 (not_21_out, eol);
  not not_22 (not_22_out, STATE[2]);
  not not_23 (not_23_out, STATE[2]);
  not not_24 (not_24_out, STATE[1]);
  and and_1 (and_1_out, STATE[2], not_1_out, STATE[0]);
  and and_2 (and_2_out, not_2_out, STATE[1], not_3_out);
  and and_3 (and_3_out, STATE[2], not_4_out, STATE[0]);
  and and_4 (x_enable, not_5_out, not_6_out, STATE[0]);
  and and_5 (and_5_out, STATE[2], not_7_out, not_8_out, gt, not_9_out);
  and and_6 (and_6_out, not_10_out, STATE[1], not_11_out);
  and and_7 (and_7_out, not_12_out, not_13_out, not_14_out, goi);
  and and_8 (and_8_out, not_15_out, STATE[1], not_16_out);
  and and_9 (and_9_out, not_17_out, not_18_out, STATE[0]);
  and and_10 (and_10_out, STATE[2], not_19_out, STATE[0]);
  and and_11 (and_11_out, STATE[2], gt, not_20_out, not_21_out, STATE[0]);
  and and_12 (and_12_out, not_22_out, STATE[1], STATE[0]);
  and and_13 (diff2_enable, not_23_out, STATE[1], STATE[0]);
  and and_14 (diff_mux, STATE[2], not_24_out, STATE[0]);
  or or_1 (diff_enable, and_1_out, and_2_out);
  or or_2 (z_enable, and_3_out, x_enable);
  or or_3 (or_3_out[0], and_5_out, and_6_out, and_7_out);
  or or_4 (or_3_out[1], and_8_out, and_9_out);
  or or_5 (or_3_out[2], and_10_out, and_11_out, and_12_out);

  assign y_enable = x_enable;
  assign z_mux = diff_mux;

  // Notes on the sheet:
  //   n1
  //   n2
  //   n0
endmodule
