// Logisim project datapath.circ as structural Verilog: 1 circuit, main circuit main
module main (
  input  diff_mux,
  input  diff_enable,
  input  [7:0] x_xi,
  input  x_enable,
  input  [7:0] y_yi,
  input  y_enable,
  input  diff2_enable,
  input  z_mux,
  input  Clock,
  input  z_enable,
  output eol,
  output gt,
  output [7:0] Z_result,
  output [7:0] diff_Result,
  output [7:0] x_Result,
  output [7:0] y_result
);

  wire comparator_1_eq, comparator_1_lt;
  wire [7:0] diff2_q, multiplexer_1_out, multiplexer_2_out, multiplier_1_out, negator_1_out, register_2_q,
       subtractor_1_out, subtractor_2_out;

  Register register_1 (.D(x_xi), .en(x_enable), .Q(x_Result), .clk(Clock));  // open: clr
  Register Y (.D(y_yi), .en(y_enable), .Q(y_result), .clk(Clock));  // open: clr
  Multiplexer #(.width(8), .enable("false")) multiplexer_1 (
    .in0(8'h1), .in1(multiplier_1_out), .out(multiplexer_1_out), .sel(z_mux));
  Register Z (.D(multiplexer_1_out), .en(z_enable), .Q(Z_result), .clk(Clock));  // open: clr
  Multiplexer #(.width(8), .enable("false")) multiplexer_2 (
    .in0(register_2_q), .in1(subtractor_2_out), .out(multiplexer_2_out), .sel(diff_mux));
  Register diff (.D(multiplexer_2_out), .en(diff_enable), .Q(diff_Result), .clk(Clock));  // open: clr
  Subtractor subtractor_1 (.a(x_Result), .b(y_result), .out(subtractor_1_out));  // open: bin, bout
  Register diff2 (.D(diff_Result), .en(diff2_enable), .Q(diff2_q), .clk(Clock));  // open: clr
  Register register_2 (.D(subtractor_1_out), .en(1'b1), .Q(register_2_q), .clk(Clock));  // open: clr
  Negator negator_1 (.in(8'h1), .out(negator_1_out));
  Multiplier multiplier_1 (.a(diff2_q), .b(Z_result), .out(multiplier_1_out));  // open: cin, cout
  Comparator comparator_1 (.a(diff_Result), .b({8{1'b0}}), .gt(gt), .eq(comparator_1_eq), .lt(comparator_1_lt));
  Subtractor subtractor_2 (.a(diff_Result), .b(negator_1_out), .out(subtractor_2_out));  // open: bin, bout
  or or_1 (eol, comparator_1_eq, comparator_1_lt);

  // Notes on the sheet:
  //   x-y
  //   z * diff2
endmodule
