// Logisim project test.circ as structural Verilog: 1 circuit, main circuit main
module main (
  input  [7:0] X,
  input  [7:0] Y_i,
  input  GO,
  output [7:0] RESULT,
  output [7:0] diff_RESULT,
  output [7:0] x_2,
  output [2:0] out_7,
  output [7:0] y
);

  wire clock_1_out, main_1_diff2_enable, main_1_diff_enable, main_1_diff_mux, main_1_x_enable,
       main_1_y_enable, main_1_z_enable, main_1_z_mux, main_2_eol, main_2_gt;

  Clock clock_1 (.out(clock_1_out));
  control_unit_main main_1 (
    .eol(main_2_eol), .gt(main_2_gt), .goi(GO), .Clock(clock_1_out), .x_enable(main_1_x_enable),
    .y_enable(main_1_y_enable), .z_enable(main_1_z_enable), .diff_enable(main_1_diff_enable),
    .diff2_enable(main_1_diff2_enable), .z_mux(main_1_z_mux), .diff_mux(main_1_diff_mux), .STATE(out_7));
  datapath_main main_2 (
    .diff_mux(main_1_diff_mux), .diff_enable(main_1_diff_enable), .x_xi(X), .x_enable(main_1_x_enable),
    .y_yi(Y_i), .y_enable(main_1_y_enable), .diff2_enable(main_1_diff2_enable), .z_mux(main_1_z_mux),
    .Clock(clock_1_out), .z_enable(main_1_z_enable), .eol(main_2_eol), .gt(main_2_gt), .Z_result(RESULT),
    .diff_Result(diff_RESULT), .x_Result(x_2), .y_result(y));
endmodule
