// Logisim project control.circ as structural Verilog: 1 circuit, main circuit Control Unit
module Control_Unit (
  input  Product,
  input  Repetation,
  input  Start,
  input  Clock,
  output left_enabled,
  output right_enabled,
  output add_multiplicand,
  output shift_product_register,
  output Counter_enabled,
  output mult_enabled,
  output Counter_Reset,
  output [2:0] Current_state
);

  wire and_1_out, and_2_out, and_3_out, and_5_out, and_6_out, and_7_out, and_8_out, and_9_out, and_10_out,
       and_11_out, and_12_out;
  wire [2:0] or_1_out;

  Register #(.width(3)) register_1 (.D(or_1_out), .en(1'b1), .Q(Current_state), .clk(Clock));  // open: clr
  and and_1 (and_1_out, ~Current_state[2], Current_state[1], ~Current_state[0], ~Product);  // AND_Gate
  and and_2 (and_2_out, ~Current_state[2], Current_state[1], Current_state[0]);  // AND_Gate
  and and_3 (and_3_out, Current_state[2], ~Current_state[1], ~Current_state[0]);  // AND_Gate
  and and_4 (mult_enabled, ~Current_state[2], ~Current_state[1], Current_state[0]);  // AND_Gate
  and and_5 (and_5_out, ~Current_state[2], Current_state[1], ~Current_state[0], Product);  // AND_Gate
  and and_6 (and_6_out, Current_state[2], ~Current_state[1], Current_state[0], Repetation);  // AND_Gate
  and and_7 (and_7_out, ~Current_state[2], ~Current_state[1], ~Current_state[0], Start);  // AND_Gate
  and and_8 (and_8_out, ~Current_state[2], Current_state[1], ~Current_state[0], Product);  // AND_Gate
  and and_9 (and_9_out, Current_state[2], ~Current_state[1], ~Current_state[0]);  // AND_Gate
  and and_10 (and_10_out, ~Current_state[2], Current_state[1], Current_state[0]);  // AND_Gate
  and and_11 (and_11_out, Current_state[2], ~Current_state[1], ~Current_state[0]);  // AND_Gate
  and and_12 (and_12_out, ~Current_state[2], ~Current_state[1], Current_state[0]);  // AND_Gate
  and and_13 (add_multiplicand, ~Current_state[2], Current_state[1], Current_state[0]);  // AND_Gate
  and and_14 (Counter_enabled, Current_state[2], ~Current_state[1], ~Current_state[0]);  // AND_Gate
  and and_15 (Counter_Reset, ~Current_state[2], ~Current_state[1], ~Current_state[0]);  // AND_Gate
  or or_1 (or_1_out[0], and_7_out, and_8_out, and_9_out);
  or or_2 (or_1_out[2], and_1_out, and_2_out, and_3_out);
  or or_3 (or_1_out[1], mult_enabled, and_5_out, and_6_out);
  or or_4 (left_enabled, mult_enabled, and_10_out, and_11_out);
  or or_5 (right_enabled, and_11_out, and_12_out);

  assign shift_product_register = Counter_enabled;

  // Notes on the sheet:
  //   s1
  //   s2
  //   s0
  //   n0
  //   n1
  //   n2
  //   n0
  //   n2
  //   n1
endmodule
