// Logisim project datapath.circ as structural Verilog: 4 circuits, main circuit Full Adder
// 0xf
module Datapath (
  input  Clock,
  input  Counter_Enable,
  input  left_enabled,
  input  add_multiplicant,
  input  [31:0] Product_Left_32_Bit,
  input  [31:0] Multiplicant,
  input  Shift_Product_Register,
  input  multiplicant_enabled,
  input  [31:0] Product_Right_32_Bit_Multiplier,
  input  right_enabled,
  input  Counter_Reset,
  output Repetetion,
  output [31:0] Left_32_bit_output,
  output [31:0] Right_32_bit_output,
  output Product0
);

  wire adder_1_overflow, comparator_1_eq, comparator_1_lt;
  wire [7:0] counter_1_q;
  wire [31:0] adder_1_result, multiplexer_1_out, multiplexer_2_out, multiplexer_3_out, register_1_q,
       shifter_1_left_32_bit_output, shifter_1_right_32_bit_output;

  Register #(.width(32)) register_1 (
    .D(Multiplicant), .en(multiplicant_enabled), .Q(register_1_q), .clk(Clock));  // open: clr
  Adder adder_1 (.A(register_1_q), .B(Left_32_bit_output), .Result(adder_1_result), .Overflow(adder_1_overflow));
  Multiplexer #(.width(32)) multiplexer_1 (
    .in0(Product_Right_32_Bit_Multiplier), .in1(shifter_1_right_32_bit_output), .out(multiplexer_1_out),
    .sel(Shift_Product_Register));  // open: en
  Multiplexer #(.width(32)) multiplexer_2 (
    .in0(Product_Left_32_Bit), .in1(adder_1_result), .out(multiplexer_2_out), .sel(add_multiplicant));  // open: en
  Register #(.width(32)) Right_32_bit (
    .D(multiplexer_1_out), .en(right_enabled), .Q({Right_32_bit_output[31:1], Product0}), .clk(Clock));  // open: clr
  Multiplexer #(.width(32)) multiplexer_3 (
    .in0(multiplexer_2_out), .in1(shifter_1_left_32_bit_output), .out(multiplexer_3_out),
    .sel(Shift_Product_Register));  // open: en
  Register #(.width(32)) Left_32_bit (
    .D(multiplexer_3_out), .en(left_enabled), .Q(Left_32_bit_output), .clk(Clock));  // open: clr
  Counter counter_1 (
    .count(Counter_Enable), .Q(counter_1_q), .clk(Clock), .clr(Counter_Reset));  // open: load, D, carry
  Shifter shifter_1 (
    .Left_32_bit(Left_32_bit_output), .Overflow(adder_1_overflow),
    .Right_32_bit({Right_32_bit_output[31:1], Product0}), .Left_32_bit_output(shifter_1_left_32_bit_output),
    .Right_32_bit_output(shifter_1_right_32_bit_output));
  Comparator comparator_1 (.a(counter_1_q), .b(8'h1f), .eq(comparator_1_eq), .lt(comparator_1_lt));  // open: gt
  or or_1 (Repetetion, comparator_1_eq, comparator_1_lt);

  assign Right_32_bit_output[0] = Product0;

  // Notes on the sheet:
  //   left + multiplicant
endmodule

module Full_Adder (
  input  Cin,
  input  Input_1,
  input  Input_2,
  output Sum,
  output Cout
);

  wire and_1_out, and_2_out, xor_1_out;

  xor xor_1 (xor_1_out, Input_1, Input_2);
  xor xor_2 (Sum, xor_1_out, Cin);
  and and_1 (and_1_out, xor_1_out, Cin);
  and and_2 (and_2_out, Input_1, Input_2);
  or or_1 (Cout, and_1_out, and_2_out);
endmodule

// Add
module Adder (
  input  [31:0] A,
  input  [31:0] B,
  output [31:0] Result,
  output Overflow
);

  wire full_adder_1_cout, full_adder_2_cout, full_adder_3_cout, full_adder_4_cout, full_adder_5_cout,
       full_adder_6_cout, full_adder_7_cout, full_adder_8_cout, full_adder_9_cout, full_adder_10_cout,
       full_adder_11_cout, full_adder_12_cout, full_adder_13_cout, full_adder_14_cout, full_adder_15_cout,
       full_adder_16_cout, full_adder_17_cout, full_adder_18_cout, full_adder_19_cout, full_adder_20_cout,
       full_adder_21_cout, full_adder_22_cout, full_adder_23_cout, full_adder_24_cout, full_adder_25_cout,
       full_adder_26_cout, full_adder_27_cout, full_adder_28_cout, full_adder_29_cout, full_adder_30_cout,
       full_adder_31_cout;

  Full_Adder full_adder_1 (.Cin(1'b0), .Input_1(A[0]), .Input_2(B[0]), .Sum(Result[0]), .Cout(full_adder_1_cout));
  Full_Adder full_adder_2 (
    .Cin(full_adder_1_cout), .Input_1(A[1]), .Input_2(B[1]), .Sum(Result[1]), .Cout(full_adder_2_cout));
  Full_Adder full_adder_3 (
    .Cin(full_adder_2_cout), .Input_1(A[2]), .Input_2(B[2]), .Sum(Result[2]), .Cout(full_adder_3_cout));
  Full_Adder full_adder_4 (
    .Cin(full_adder_3_cout), .Input_1(A[3]), .Input_2(B[3]), .Sum(Result[3]), .Cout(full_adder_4_cout));
  Full_Adder full_adder_5 (
    .Cin(full_adder_4_cout), .Input_1(A[4]), .Input_2(B[4]), .Sum(Result[4]), .Cout(full_adder_5_cout));
  Full_Adder full_adder_6 (
    .Cin(full_adder_5_cout), .Input_1(A[5]), .Input_2(B[5]), .Sum(Result[5]), .Cout(full_adder_6_cout));
  Full_Adder full_adder_7 (
    .Cin(full_adder_6_cout), .Input_1(A[6]), .Input_2(B[6]), .Sum(Result[6]), .Cout(full_adder_7_cout));
  Full_Adder full_adder_8 (
    .Cin(full_adder_7_cout), .Input_1(A[7]), .Input_2(B[7]), .Sum(Result[7]), .Cout(full_adder_8_cout));
  Full_Adder full_adder_9 (
    .Cin(full_adder_8_cout), .Input_1(A[8]), .Input_2(B[8]), .Sum(Result[8]), .Cout(full_adder_9_cout));
  Full_Adder full_adder_10 (
    .Cin(full_adder_9_cout), .Input_1(A[9]), .Input_2(B[9]), .Sum(Result[9]), .Cout(full_adder_10_cout));
  Full_Adder full_adder_11 (
    .Cin(full_adder_10_cout), .Input_1(A[10]), .Input_2(B[10]), .Sum(Result[10]), .Cout(full_adder_11_cout));
  Full_Adder full_adder_12 (
    .Cin(full_adder_11_cout), .Input_1(A[11]), .Input_2(B[11]), .Sum(Result[11]), .Cout(full_adder_12_cout));
  Full_Adder full_adder_13 (
    .Cin(full_adder_12_cout), .Input_1(A[12]), .Input_2(B[12]), .Sum(Result[12]), .Cout(full_adder_13_cout));
  Full_Adder full_adder_14 (
    .Cin(full_adder_13_cout), .Input_1(A[13]), .Input_2(B[13]), .Sum(Result[13]), .Cout(full_adder_14_cout));
  Full_Adder full_adder_15 (
    .Cin(full_adder_14_cout), .Input_1(A[14]), .Input_2(B[14]), .Sum(Result[14]), .Cout(full_adder_15_cout));
  Full_Adder full_adder_16 (
    .Cin(full_adder_15_cout), .Input_1(A[15]), .Input_2(B[15]), .Sum(Result[15]), .Cout(full_adder_16_cout));
  Full_Adder full_adder_17 (
    .Cin(full_adder_16_cout), .Input_1(A[16]), .Input_2(B[16]), .Sum(Result[16]), .Cout(full_adder_17_cout));
  Full_Adder full_adder_18 (
    .Cin(full_adder_17_cout), .Input_1(A[17]), .Input_2(B[17]), .Sum(Result[17]), .Cout(full_adder_18_cout));
  Full_Adder full_adder_19 (
    .Cin(full_adder_18_cout), .Input_1(A[18]), .Input_2(B[18]), .Sum(Result[18]), .Cout(full_adder_19_cout));
  Full_Adder full_adder_20 (
    .Cin(full_adder_19_cout), .Input_1(A[19]), .Input_2(B[19]), .Sum(Result[19]), .Cout(full_adder_20_cout));
  Full_Adder full_adder_21 (
    .Cin(full_adder_20_cout), .Input_1(A[20]), .Input_2(B[20]), .Sum(Result[20]), .Cout(full_adder_21_cout));
  Full_Adder full_adder_22 (
    .Cin(full_adder_21_cout), .Input_1(A[21]), .Input_2(B[21]), .Sum(Result[21]), .Cout(full_adder_22_cout));
  Full_Adder full_adder_23 (
    .Cin(full_adder_22_cout), .Input_1(A[22]), .Input_2(B[22]), .Sum(Result[22]), .Cout(full_adder_23_cout));
  Full_Adder full_adder_24 (
    .Cin(full_adder_23_cout), .Input_1(A[23]), .Input_2(B[23]), .Sum(Result[23]), .Cout(full_adder_24_cout));
  Full_Adder full_adder_25 (
    .Cin(full_adder_24_cout), .Input_1(A[24]), .Input_2(B[24]), .Sum(Result[24]), .Cout(full_adder_25_cout));
  Full_Adder full_adder_26 (
    .Cin(full_adder_25_cout), .Input_1(A[25]), .Input_2(B[25]), .Sum(Result[25]), .Cout(full_adder_26_cout));
  Full_Adder full_adder_27 (
    .Cin(full_adder_26_cout), .Input_1(A[26]), .Input_2(B[26]), .Sum(Result[26]), .Cout(full_adder_27_cout));
  Full_Adder full_adder_28 (
    .Cin(full_adder_27_cout), .Input_1(A[27]), .Input_2(B[27]), .Sum(Result[27]), .Cout(full_adder_28_cout));
  Full_Adder full_adder_29 (
    .Cin(full_adder_28_cout), .Input_1(A[28]), .Input_2(B[28]), .Sum(Result[28]), .Cout(full_adder_29_cout));
  Full_Adder full_adder_30 (
    .Cin(full_adder_29_cout), .Input_1(A[29]), .Input_2(B[29]), .Sum(Result[29]), .Cout(full_adder_30_cout));
  Full_Adder full_adder_31 (
    .Cin(full_adder_30_cout), .Input_1(A[30]), .Input_2(B[30]), .Sum(Result[30]), .Cout(full_adder_31_cout));
  Full_Adder full_adder_32 (
    .Cin(full_adder_31_cout), .Input_1(A[31]), .Input_2(B[31]), .Sum(Result[31]), .Cout(Overflow));
endmodule

module Shifter (
  input  [31:0] Left_32_bit,
  input  Overflow,
  input  [31:0] Right_32_bit,
  output [31:0] Left_32_bit_output,
  output [31:0] Right_32_bit_output
);


  assign Left_32_bit_output = {Overflow, Left_32_bit[31:1]};
  assign Right_32_bit_output = {Left_32_bit[0], Right_32_bit[31:1]};
endmodule
