// Logisim project mult32.circ as structural Verilog: 1 circuit, main circuit main
module main (
  input  [31:0] Product_Left_32_Bit,
  input  [31:0] Product_Right_32_Bit_Multiplier,
  input  [31:0] Multiplicant,
  output [31:0] Product_Left_32_Bit_Output,
  output [31:0] Product_Right__32_Bit_Output,
  output [2:0] out_6
);

  wire Calculate_out, clock_1_out, control_unit_1_add_multiplicand, control_unit_1_counter_enabled,
       control_unit_1_counter_reset, control_unit_1_left_enabled, control_unit_1_mult_enabled,
       control_unit_1_right_enabled, control_unit_1_shift_product_register, datapath_1_product0,
       datapath_1_repetetion;

  Button Calculate (.out(Calculate_out));
  Clock clock_1 (.out(clock_1_out));
  Control_Unit control_unit_1 (
    .Product(datapath_1_product0), .Repetation(datapath_1_repetetion), .Start(Calculate_out),
    .Clock(clock_1_out), .left_enabled(control_unit_1_left_enabled),
    .right_enabled(control_unit_1_right_enabled), .add_multiplicand(control_unit_1_add_multiplicand),
    .shift_product_register(control_unit_1_shift_product_register),
    .Counter_enabled(control_unit_1_counter_enabled), .mult_enabled(control_unit_1_mult_enabled),
    .Counter_Reset(control_unit_1_counter_reset), .Current_state(out_6));
  Datapath datapath_1 (
    .Clock(clock_1_out), .Counter_Enable(control_unit_1_counter_enabled),
    .left_enabled(control_unit_1_left_enabled), .add_multiplicant(control_unit_1_add_multiplicand),
    .Product_Left_32_Bit(Product_Left_32_Bit), .Multiplicant(Multiplicant),
    .Shift_Product_Register(control_unit_1_shift_product_register),
    .multiplicant_enabled(control_unit_1_mult_enabled),
    .Product_Right_32_Bit_Multiplier(Product_Right_32_Bit_Multiplier),
    .right_enabled(control_unit_1_right_enabled), .Counter_Reset(control_unit_1_counter_reset),
    .Repetetion(datapath_1_repetetion), .Left_32_bit_output(Product_Left_32_Bit_Output),
    .Right_32_bit_output(Product_Right__32_Bit_Output), .Product0(datapath_1_product0));
endmodule
